// Logisim project 实验电路.circ as structural Verilog: 16 circuits, main circuit ◇多周期MIPS(微程序)
module \单周期MIPS_硬布线  (
);

  wire and_1_out, and_2_out, CLK, mips_alu_1_equal, not_1_out, not_2_out, or_1_out, RST,
       \单周期硬布线控制器_1_alusrc , \单周期硬布线控制器_1_beq , \单周期硬布线控制器_1_bne , \单周期硬布线控制器_1_halt ,
       \单周期硬布线控制器_1_memtoreg , \单周期硬布线控制器_1_memwrite , \单周期硬布线控制器_1_regdst , \单周期硬布线控制器_1_regwrite ;
  wire [3:0] \单周期硬布线控制器_1_alu_op ;
  wire [4:0] multiplexer_2_out;
  wire [31:0] adder_1_out, adder_2_out, bit_extender_1_out, mips_alu_1_result, mips_regifile_1_r1,
       mips_regifile_1_r2, multiplexer_1_out, multiplexer_3_out, multiplexer_4_out, PC_q, ram_1_data,
       rom_1_data, shifter_1_out, \总周期数 ;

  Button \u_总复位  (.out(RST));
  Multiplexer #(.width(32), .enable("false")) multiplexer_1 (
    .in0(adder_1_out), .in1(adder_2_out), .out(multiplexer_1_out), .sel(or_1_out));
  Register #(.width(32)) PC (.D(multiplexer_1_out), .en(not_1_out), .Q(PC_q), .clk(CLK), .clr(RST));
  not not_1 (not_1_out, \单周期硬布线控制器_1_halt );
  Counter #(.width(32), .max('hffffffff)) counter_1 (
    .count(not_1_out), .Q(\总周期数 ), .clk(CLK), .clr(RST));  // open: load, D, carry
  Adder #(.width(32)) adder_1 (.a(PC_q), .b(32'h4), .out(adder_1_out));  // open: cin, cout
  Clock clock_1 (.out(CLK));
  ROM #(.addrWidth(10), .dataWidth(32)) rom_1 (.addr(PC_q[11:2]), .data(rom_1_data));  // open: sel
  \单周期硬布线控制器  \u_单周期硬布线控制器_1  (
    .OP(rom_1_data[31:26]), .Func(rom_1_data[5:0]), .ALU_OP(\单周期硬布线控制器_1_alu_op ),
    .RegDst(\单周期硬布线控制器_1_regdst ), .RegWrite(\单周期硬布线控制器_1_regwrite ), .MemToReg(\单周期硬布线控制器_1_memtoreg ),
    .MemWrite(\单周期硬布线控制器_1_memwrite ), .AluSrc(\单周期硬布线控制器_1_alusrc ), .Beq(\单周期硬布线控制器_1_beq ),
    .Bne(\单周期硬布线控制器_1_bne ), .Halt(\单周期硬布线控制器_1_halt ));
  Multiplexer #(.width(5), .enable("false")) multiplexer_2 (
    .in0(rom_1_data[20:16]), .in1(rom_1_data[15:11]), .out(multiplexer_2_out), .sel(\单周期硬布线控制器_1_regdst ));
  assign bit_extender_1_out = {{16{rom_1_data[15]}}, rom_1_data[15:0]};  // Bit_Extender bit_extender_1
  // Probe on \总周期数 
  MIPS_Regifile mips_regifile_1 (
    .Din(multiplexer_4_out), .Clk(CLK), .R1(mips_regifile_1_r1), .R2(mips_regifile_1_r2),
    .WE(\单周期硬布线控制器_1_regwrite ), .W_num(multiplexer_2_out), .R1_num(rom_1_data[25:21]),
    .R2_num(rom_1_data[20:16]));
  Multiplexer #(.width(32), .enable("false")) multiplexer_3 (
    .in0(mips_regifile_1_r2), .in1(bit_extender_1_out), .out(multiplexer_3_out), .sel(\单周期硬布线控制器_1_alusrc ));
  MIPS_ALU mips_alu_1 (
    .X(mips_regifile_1_r1), .Y(multiplexer_3_out), .AluOP(\单周期硬布线控制器_1_alu_op ), .Equal(mips_alu_1_equal),
    .Result(mips_alu_1_result));  // open: Result_2
  Shifter #(.width(32)) shifter_1 (.in(bit_extender_1_out), .\dist (5'b00010), .out(shifter_1_out));
  Adder #(.width(32)) adder_2 (.a(shifter_1_out), .b(adder_1_out), .out(adder_2_out));  // open: cin, cout
  and and_1 (and_1_out, \单周期硬布线控制器_1_beq , mips_alu_1_equal);
  and and_2 (and_2_out, \单周期硬布线控制器_1_bne , not_2_out);
  not not_2 (not_2_out, mips_alu_1_equal);
  or or_1 (or_1_out, and_1_out, and_2_out);
  RAM #(.addrWidth(10), .dataWidth(32), .bus("separate")) ram_1 (
    .addr(mips_alu_1_result[11:2]), .din(mips_regifile_1_r2), .data(ram_1_data),
    .str(\单周期硬布线控制器_1_memwrite ), .clk(CLK), .clr(RST));  // open: sel, ld
  Multiplexer #(.width(32), .enable("false")) multiplexer_4 (
    .in0(mips_alu_1_result), .in1(ram_1_data), .out(multiplexer_4_out), .sel(\单周期硬布线控制器_1_memtoreg ));

  // Notes on the sheet:
  //   指令存储器
  //   Ctrl+K  Command+K触发时钟连续仿真，程序运行结束后可停机，查看数据存储器中80单元的排序情况是有符号降序
  //   contents of rom_1 (hex, n*v repeats v):
  //   2010ffff 20110000 ae300200 22100001 22310004 ae300200 22100001 22310004 ae300200 22100001 22310004
  //   ae300200 22100001 22310004 ae300200 22100001 22310004 ae300200 22100001 22310004 ae300200 22100001
  //   22310004 ae300200 8020 2011001c 8e130200 8e340200 274402a 11000002 ae330200 ae140200 2231fffc
  //   1611fff8 22100004 2011001c 1611fff5 2002000a c
  //   总周期数参考值：224
  //   Halt
  //   Op
  //   Func
  //   RegDst
  //   MemToReg
  //   MemWrite
  //   Beq
  //   Bne
  //   AluOP
  //   AluSrcB
  //   RegWrite
endmodule

// 单周期硬布线控制器
module \单周期硬布线控制器  (
  input  [5:0] OP,
  input  [5:0] Func,
  output [3:0] ALU_OP,
  output RegDst,
  output RegWrite,
  output MemToReg,
  output MemWrite,
  output AluSrc,
  output Beq,
  output Bne,
  output Halt
);

  wire ADD, ADDI, comparator_6_eq, comparator_7_eq, comparator_8_eq, comparator_9_eq, SLT;
  wire [1:0] or_5_out;

  Comparator #(.width(6)) comparator_1 (.a(OP), .b(6'b100011), .eq(MemToReg));  // open: gt, lt
  Comparator #(.width(6)) comparator_2 (.a(OP), .b(6'b101011), .eq(MemWrite));  // open: gt, lt
  Comparator #(.width(6)) comparator_3 (.a(OP), .b(6'b000100), .eq(Beq));  // open: gt, lt
  Comparator #(.width(6)) comparator_4 (.a(OP), .b(6'b000101), .eq(Bne));  // open: gt, lt
  Comparator #(.width(6)) comparator_5 (.a(OP), .b(6'b001000), .eq(ADDI));  // open: gt, lt
  Comparator #(.width(6)) comparator_6 (.a(OP), .b({6{1'b0}}), .eq(comparator_6_eq));  // open: gt, lt
  Comparator #(.width(6)) comparator_7 (.a(Func), .b(6'b100000), .eq(comparator_7_eq));  // open: gt, lt
  Comparator #(.width(6)) comparator_8 (.a(Func), .b(6'b101010), .eq(comparator_8_eq));  // open: gt, lt
  Comparator #(.width(6)) comparator_9 (.a(Func), .b(6'b001100), .eq(comparator_9_eq));  // open: gt, lt
  or or_1 (RegWrite, RegDst, ADDI, MemToReg);
  and and_1 (ADD, comparator_7_eq, comparator_6_eq);
  and and_2 (SLT, comparator_8_eq, comparator_6_eq);
  and and_3 (Halt, comparator_9_eq, comparator_6_eq);
  or or_2 (RegDst, ADD, SLT);
  or or_3 (AluSrc, ADDI, MemToReg, MemWrite);
  or or_4 (or_5_out[1], SLT, Beq, Bne);
  or or_5 (or_5_out[0], ADDI, ADD, MemWrite, MemToReg);
  Multiplexer #(.select(2), .width(4), .enable("false")) multiplexer_1 (
    .in0(4'b0000), .in1(4'b0101), .in2(4'b1011), .in3(4'b0000), .out(ALU_OP), .sel(or_5_out));

  // Other names for the same wires on the sheet: LW = MemToReg; R_TYPE = RegDst; SW = MemWrite; SysCall = Halt

  // Notes on the sheet:
  //   指令译码信号
  //   指令译码逻辑
  //   给出简单的逻辑实现对应指令译码信号，LW、SW、BEQ、BNE、ADDI、ADD、SLT、SYSCALL、R_TYPE。
  //   ALU控制器逻辑
  //   注意R_TYPE表示R型运算指令，SYSCALL是特殊的R型指令，不属于这个类别
  //   给出简单的逻辑实现ALU_OP与OP、Func之间的对应关系
  //   控制信号
  //   根据指令译码信号实现控制器输出控制信号的逻辑
endmodule

module \多周期MIPS_微程序  (
);

  wire and_1_out, and_2_out, CLK, comparator_1_eq, mips_alu_1_equal, not_1_out, not_2_out, or_1_out, RST,
       \多周期微程序控制器_1_alusrca , \多周期微程序控制器_1_beq , \多周期微程序控制器_1_bne , \多周期微程序控制器_1_iord ,
       \多周期微程序控制器_1_irwrite , \多周期微程序控制器_1_memread , \多周期微程序控制器_1_memtoreg , \多周期微程序控制器_1_memwrite ,
       \多周期微程序控制器_1_pcsrc , \多周期微程序控制器_1_pcwrite , \多周期微程序控制器_1_regdst , \多周期微程序控制器_1_regwrite ;
  wire [1:0] \多周期微程序控制器_1_alusrcb ;
  wire [3:0] \多周期微程序控制器_1_alu_op , \多周期微程序控制器_1_当前微指令地址 ;
  wire [4:0] multiplexer_2_out;
  wire [15:0] \总周期数 ;
  wire [31:0] A_q, B_q, bit_extender_1_out, C_q, DR_q, IR_q, mips_alu_1_result, mips_regifile_1_r1,
       mips_regifile_1_r2, multiplexer_1_out, multiplexer_3_out, multiplexer_4_out, multiplexer_5_out,
       multiplexer_6_out, PC_q, ram_1_data, shifter_1_out;

  Button \u_总复位  (.out(RST));
  Clock clock_1 (.out(CLK));
  Register #(.width(32)) PC (.D(multiplexer_6_out), .en(or_1_out), .Q(PC_q), .clk(CLK), .clr(RST));
  Multiplexer #(.width(32), .enable("false")) multiplexer_1 (
    .in0(PC_q), .in1(C_q), .out(multiplexer_1_out), .sel(\多周期微程序控制器_1_iord ));
  RAM #(.addrWidth(10), .dataWidth(32), .bus("separate")) ram_1 (
    .addr(multiplexer_1_out[11:2]), .din(B_q), .data(ram_1_data), .str(\多周期微程序控制器_1_memwrite ), .clk(CLK),
    .ld(\多周期微程序控制器_1_memread ));  // open: sel, clr
  // Probe on \总周期数 
  Register #(.width(32)) IR (.D(ram_1_data), .en(\多周期微程序控制器_1_irwrite ), .Q(IR_q), .clk(CLK), .clr(RST));
  Register #(.width(32)) DR (.D(ram_1_data), .Q(DR_q), .clk(CLK), .clr(RST));  // open: en
  // Probe on \多周期微程序控制器_1_当前微指令地址 
  \多周期微程序控制器  \u_多周期微程序控制器_1  (
    .PcWrite(\多周期微程序控制器_1_pcwrite ), .Beq(\多周期微程序控制器_1_beq ), .PCsrc(\多周期微程序控制器_1_pcsrc ),
    .AluSrcB(\多周期微程序控制器_1_alusrcb ), .AluSrcA(\多周期微程序控制器_1_alusrca ), .RegWrite(\多周期微程序控制器_1_regwrite ),
    .MemToReg(\多周期微程序控制器_1_memtoreg ), .RegDst(\多周期微程序控制器_1_regdst ), .IorD(\多周期微程序控制器_1_iord ),
    .MemWrite(\多周期微程序控制器_1_memwrite ), .MemRead(\多周期微程序控制器_1_memread ), .IrWrite(\多周期微程序控制器_1_irwrite ),
    .Bne(\多周期微程序控制器_1_bne ), .CLK(CLK), .\当前微指令地址 (\多周期微程序控制器_1_当前微指令地址 ), .RST(RST), .OP(IR_q[31:26]),
    .ALU_OP(\多周期微程序控制器_1_alu_op ), .Func(IR_q[5:0]));
  Multiplexer #(.width(5), .enable("false")) multiplexer_2 (
    .in0(IR_q[20:16]), .in1(IR_q[15:11]), .out(multiplexer_2_out), .sel(\多周期微程序控制器_1_regdst ));
  Multiplexer #(.width(32), .enable("false")) multiplexer_3 (
    .in0(C_q), .in1(DR_q), .out(multiplexer_3_out), .sel(\多周期微程序控制器_1_memtoreg ));
  Comparator #(.width(4)) comparator_1 (.a(4'b1101), .b(\多周期微程序控制器_1_当前微指令地址 ), .eq(comparator_1_eq));  // open: gt, lt
  not not_1 (not_1_out, comparator_1_eq);
  assign bit_extender_1_out = {{16{IR_q[15]}}, IR_q[15:0]};  // Bit_Extender bit_extender_1
  Counter #(.width(16), .max('hffff)) counter_1 (
    .count(not_1_out), .Q(\总周期数 ), .clk(CLK), .clr(RST));  // open: load, D, carry
  MIPS_Regifile mips_regifile_1 (
    .Din(multiplexer_3_out), .Clk(CLK), .R1(mips_regifile_1_r1), .R2(mips_regifile_1_r2),
    .WE(\多周期微程序控制器_1_regwrite ), .W_num(multiplexer_2_out), .R1_num(IR_q[25:21]), .R2_num(IR_q[20:16]));
  Register #(.width(32)) A (.D(mips_regifile_1_r1), .Q(A_q), .clk(CLK), .clr(RST));  // open: en
  Register #(.width(32)) B (.D(mips_regifile_1_r2), .Q(B_q), .clk(CLK), .clr(RST));  // open: en
  Shifter #(.width(32)) shifter_1 (.in(bit_extender_1_out), .\dist (5'b00010), .out(shifter_1_out));
  Multiplexer #(.width(32), .enable("false")) multiplexer_4 (
    .in0(PC_q), .in1(A_q), .out(multiplexer_4_out), .sel(\多周期微程序控制器_1_alusrca ));
  Multiplexer #(.select(2), .width(32), .enable("false")) multiplexer_5 (
    .in0(B_q), .in1(32'h4), .in2(bit_extender_1_out), .in3(shifter_1_out), .out(multiplexer_5_out),
    .sel(\多周期微程序控制器_1_alusrcb ));
  not not_2 (not_2_out, mips_alu_1_equal);
  MIPS_ALU mips_alu_1 (
    .X(multiplexer_4_out), .Y(multiplexer_5_out), .AluOP(\多周期微程序控制器_1_alu_op ), .Equal(mips_alu_1_equal),
    .Result(mips_alu_1_result));  // open: Result_2
  and and_1 (and_1_out, \多周期微程序控制器_1_beq , mips_alu_1_equal);
  and and_2 (and_2_out, \多周期微程序控制器_1_bne , not_2_out);
  Register #(.width(32)) C (.D(mips_alu_1_result), .Q(C_q), .clk(CLK), .clr(RST));  // open: en
  or or_1 (or_1_out, \多周期微程序控制器_1_pcwrite , and_1_out, and_2_out);
  Multiplexer #(.width(32), .enable("false")) multiplexer_6 (
    .in0(mips_alu_1_result), .in1(C_q), .out(multiplexer_6_out), .sel(\多周期微程序控制器_1_pcsrc ));

  // Notes on the sheet:
  //   Ctrl+K  Command+K触发时钟连续仿真，程序运行结束后可停机，查看数据存储器中80单元的排序情况是有符号降序
  //   存储器
  //   总周期数参考值：891
  //   IorD
  //   MemWrite
  //   MemRead
  //   IRWrite
  //   OP
  //   Func
  //   RegDst
  //   PcWrite
  //   Beq
  //   Bne
  //   PcSrc
  //   AluOP
  //   AluSrcB
  //   AluSrcA
  //   RegWrite
  //   MemToReg
endmodule

// 微程序控制器
module \多周期微程序控制器  (
  input  [5:0] OP,
  input  [5:0] Func,
  input  CLK,
  input  RST,
  output [3:0] ALU_OP,
  output Bne,
  output Beq,
  output MemRead,
  output MemWrite,
  output RegWrite,
  output PcWrite,
  output IrWrite,
  output RegDst,
  output MemToReg,
  output [3:0] \当前微指令地址 ,
  output [1:0] AluSrcB,
  output AluSrcA,
  output PCsrc,
  output IorD
);

  wire ADD, ADDI, BEQ_t, BNE_t, comparator_6_eq, comparator_7_eq, comparator_8_eq, comparator_9_eq, LW, P,
       R_TYPE, SLT, SW, SysCall;
  wire [1:0] ALU_Control;
  wire [3:0] multiplexer_1_out, multiplexer_2_out, rom_1_data, \微程序地址转移逻辑_1_s0 ;

  Comparator #(.width(6)) comparator_1 (.a(OP), .b(6'b100011), .eq(LW));  // open: gt, lt
  Comparator #(.width(6)) comparator_2 (.a(OP), .b(6'b101011), .eq(SW));  // open: gt, lt
  Comparator #(.width(6)) comparator_3 (.a(OP), .b(6'b000100), .eq(BEQ_t));  // open: gt, lt
  Comparator #(.width(6)) comparator_4 (.a(OP), .b(6'b000101), .eq(BNE_t));  // open: gt, lt
  Comparator #(.width(6)) comparator_5 (.a(OP), .b(6'b001000), .eq(ADDI));  // open: gt, lt
  Comparator #(.width(6)) comparator_6 (.a(OP), .b({6{1'b0}}), .eq(comparator_6_eq));  // open: gt, lt
  \微程序地址转移逻辑  \u_微程序地址转移逻辑_1  (
    .R_Type(R_TYPE), .S3(\微程序地址转移逻辑_1_s0 [3]), .ADDI(ADDI), .S2(\微程序地址转移逻辑_1_s0 [2]), .LW(LW),
    .S1(\微程序地址转移逻辑_1_s0 [1]), .SW(SW), .S0(\微程序地址转移逻辑_1_s0 [0]), .BEQ(BEQ_t), .BNE(BNE_t), .SYSCALL(SysCall));
  Comparator #(.width(6)) comparator_7 (.a(Func), .b(6'b100000), .eq(comparator_7_eq));  // open: gt, lt
  Comparator #(.width(6)) comparator_8 (.a(Func), .b(6'b101010), .eq(comparator_8_eq));  // open: gt, lt
  Comparator #(.width(6)) comparator_9 (.a(Func), .b(6'b001100), .eq(comparator_9_eq));  // open: gt, lt
  and and_1 (ADD, comparator_7_eq, comparator_6_eq);
  and and_2 (SLT, comparator_8_eq, comparator_6_eq);
  and and_3 (SysCall, comparator_9_eq, comparator_6_eq);
  Multiplexer #(.width(4), .enable("false")) multiplexer_1 (
    .in0(rom_1_data), .in1(\微程序地址转移逻辑_1_s0 ), .out(multiplexer_1_out), .sel(P));
  Register #(.width(4)) register_1 (.D(multiplexer_1_out), .Q(\当前微指令地址 ), .clk(CLK), .clr(RST));  // open: en
  or or_1 (R_TYPE, ADD, SLT);
  ROM #(.addrWidth(4), .dataWidth(21)) rom_1 (
    .addr(\当前微指令地址 ),
    .data({IorD, PCsrc, AluSrcA, AluSrcB, MemToReg, RegDst, IrWrite, PcWrite, RegWrite, MemWrite, MemRead, Beq, Bne, ALU_Control, P, rom_1_data}));  // open: sel
  Multiplexer #(.select(2), .width(4), .enable("false")) multiplexer_2 (
    .in0(4'b0000), .in1(4'b0101), .in2(4'b1011), .in3(4'b0000), .out(multiplexer_2_out), .sel({SLT, ADD}));
  Multiplexer #(.select(2), .width(4), .enable("false")) multiplexer_3 (
    .in0(4'b0101), .in1(4'b0110), .in2(multiplexer_2_out), .in3(4'b0000), .out(ALU_OP), .sel(ALU_Control));

  // Notes on the sheet:
  //   指令译码信号
  //   根据指令进行微程序地址转移
  //   指令译码逻辑
  //   给出简单的逻辑实现对应指令译码信号，LW、SW、BEQ、BNE、ADDI、ADD、SLT、SYSCALL、R_TYPE。
  //   下址字段
  //   微程序
  //   入口地址
  //   判断逻辑
  //   μAR
  //   控制存储器
  //   contents of rom_1 (hex, n*v repeats v):
  //   13201 30010 60003 110204 18800 60006 110400 40048 14840 c0100 c0080 6000c 10800 1000d
  //   微命令
  //   ALU控制器逻辑
  //   根据ALU_Control的值决定运算器运算选择控制信号ALU_OP的值
  //   注意R_TYPE表示R型运算指令，SYSCALL是特殊的R型指令，不属于这个类别
  //   微指令
  //   下址字段
  //   判断逻辑
  //   ALU_Control= 00 运算器做加法
  //   ALU_Control= 01 运算器做减法
  //   ALU_Control= 10 运算方式由Func决定 
endmodule

// 地址转移逻辑
module \微程序地址转移逻辑  (
  input  R_Type,
  input  ADDI,
  input  LW,
  input  SW,
  input  BEQ,
  input  BNE,
  input  SYSCALL,
  output S3,
  output S2,
  output S1,
  output S0
);

  or or_1 (S3, ADDI, BEQ, BNE, SYSCALL);
  or or_2 (S2, R_Type, SW, SYSCALL);
  or or_3 (S1, R_Type, ADDI, LW, BNE);
  or or_4 (S0, R_Type, ADDI, SW, BEQ, SYSCALL);
endmodule

module \多周期MIPS_硬布线  (
);

  wire and_1_out, and_2_out, CLK, comparator_1_eq, mips_alu_1_equal, not_1_out, not_2_out, or_1_out, RST,
       \多周期硬布线控制器_1_alusrca , \多周期硬布线控制器_1_beq , \多周期硬布线控制器_1_bne , \多周期硬布线控制器_1_iord ,
       \多周期硬布线控制器_1_irwrite , \多周期硬布线控制器_1_memread , \多周期硬布线控制器_1_memtoreg , \多周期硬布线控制器_1_memwrite ,
       \多周期硬布线控制器_1_pcsrc , \多周期硬布线控制器_1_pcwrite , \多周期硬布线控制器_1_regdst , \多周期硬布线控制器_1_regwrite ;
  wire [1:0] \多周期硬布线控制器_1_alusrcb ;
  wire [3:0] \多周期硬布线控制器_1_alu_op , \多周期硬布线控制器_1_当前状态 ;
  wire [4:0] multiplexer_2_out;
  wire [15:0] \总周期数 ;
  wire [31:0] A_q, B_q, bit_extender_1_out, C_q, DR_q, IR_q, mips_alu_1_result, mips_regifile_1_r1,
       mips_regifile_1_r2, multiplexer_1_out, multiplexer_3_out, multiplexer_4_out, multiplexer_5_out,
       multiplexer_6_out, PC_q, ram_1_data, shifter_1_out;

  Button \u_总复位  (.out(RST));
  Register #(.width(32)) PC (.D(multiplexer_6_out), .en(or_1_out), .Q(PC_q), .clk(CLK), .clr(RST));
  Clock clock_1 (.out(CLK));
  Multiplexer #(.width(32), .enable("false")) multiplexer_1 (
    .in0(PC_q), .in1(C_q), .out(multiplexer_1_out), .sel(\多周期硬布线控制器_1_iord ));
  RAM #(.addrWidth(10), .dataWidth(32), .bus("separate")) ram_1 (
    .addr(multiplexer_1_out[11:2]), .din(B_q), .data(ram_1_data), .str(\多周期硬布线控制器_1_memwrite ), .clk(CLK),
    .ld(\多周期硬布线控制器_1_memread ));  // open: sel, clr
  // Probe on \总周期数 
  Register #(.width(32)) IR (.D(ram_1_data), .en(\多周期硬布线控制器_1_irwrite ), .Q(IR_q), .clk(CLK), .clr(RST));
  Register #(.width(32)) DR (.D(ram_1_data), .Q(DR_q), .clk(CLK), .clr(RST));  // open: en
  // Probe on \多周期硬布线控制器_1_当前状态 
  Multiplexer #(.width(5), .enable("false")) multiplexer_2 (
    .in0(IR_q[20:16]), .in1(IR_q[15:11]), .out(multiplexer_2_out), .sel(\多周期硬布线控制器_1_regdst ));
  assign bit_extender_1_out = {{16{IR_q[15]}}, IR_q[15:0]};  // Bit_Extender bit_extender_1
  \多周期硬布线控制器  \u_多周期硬布线控制器_1  (
    .AluSrcB(\多周期硬布线控制器_1_alusrcb ), .OP(IR_q[31:26]), .Func(IR_q[5:0]), .ALU_OP(\多周期硬布线控制器_1_alu_op ),
    .CLK(CLK), .RST(RST), .\当前状态 (\多周期硬布线控制器_1_当前状态 ), .IorD(\多周期硬布线控制器_1_iord ),
    .PCsrc(\多周期硬布线控制器_1_pcsrc ), .AluSrcA(\多周期硬布线控制器_1_alusrca ), .MemToReg(\多周期硬布线控制器_1_memtoreg ),
    .RegDst(\多周期硬布线控制器_1_regdst ), .IrWrite(\多周期硬布线控制器_1_irwrite ), .PcWrite(\多周期硬布线控制器_1_pcwrite ),
    .RegWrite(\多周期硬布线控制器_1_regwrite ), .MemWrite(\多周期硬布线控制器_1_memwrite ), .MemRead(\多周期硬布线控制器_1_memread ),
    .Beq(\多周期硬布线控制器_1_beq ), .Bne(\多周期硬布线控制器_1_bne ));
  Multiplexer #(.width(32), .enable("false")) multiplexer_3 (
    .in0(C_q), .in1(DR_q), .out(multiplexer_3_out), .sel(\多周期硬布线控制器_1_memtoreg ));
  Comparator #(.width(4)) comparator_1 (.a(4'b1101), .b(\多周期硬布线控制器_1_当前状态 ), .eq(comparator_1_eq));  // open: gt, lt
  MIPS_Regifile mips_regifile_1 (
    .Din(multiplexer_3_out), .Clk(CLK), .R1(mips_regifile_1_r1), .R2(mips_regifile_1_r2),
    .WE(\多周期硬布线控制器_1_regwrite ), .W_num(multiplexer_2_out), .R1_num(IR_q[25:21]), .R2_num(IR_q[20:16]));
  Counter #(.width(16), .max('hffff)) counter_1 (
    .count(not_1_out), .Q(\总周期数 ), .clk(CLK), .clr(RST));  // open: load, D, carry
  not not_1 (not_1_out, comparator_1_eq);
  Register #(.width(32)) A (.D(mips_regifile_1_r1), .Q(A_q), .clk(CLK), .clr(RST));  // open: en
  Register #(.width(32)) B (.D(mips_regifile_1_r2), .Q(B_q), .clk(CLK), .clr(RST));  // open: en
  Multiplexer #(.width(32), .enable("false")) multiplexer_4 (
    .in0(PC_q), .in1(A_q), .out(multiplexer_4_out), .sel(\多周期硬布线控制器_1_alusrca ));
  Shifter #(.width(32)) shifter_1 (.in(bit_extender_1_out), .\dist (5'b00010), .out(shifter_1_out));
  Multiplexer #(.select(2), .width(32), .enable("false")) multiplexer_5 (
    .in0(B_q), .in1(32'h4), .in2(bit_extender_1_out), .in3(shifter_1_out), .out(multiplexer_5_out),
    .sel(\多周期硬布线控制器_1_alusrcb ));
  MIPS_ALU mips_alu_1 (
    .X(multiplexer_4_out), .Y(multiplexer_5_out), .AluOP(\多周期硬布线控制器_1_alu_op ), .Equal(mips_alu_1_equal),
    .Result(mips_alu_1_result));  // open: Result_2
  not not_2 (not_2_out, mips_alu_1_equal);
  Register #(.width(32)) C (.D(mips_alu_1_result), .Q(C_q), .clk(CLK), .clr(RST));  // open: en
  and and_1 (and_1_out, \多周期硬布线控制器_1_beq , mips_alu_1_equal);
  and and_2 (and_2_out, \多周期硬布线控制器_1_bne , not_2_out);
  Multiplexer #(.width(32), .enable("false")) multiplexer_6 (
    .in0(mips_alu_1_result), .in1(C_q), .out(multiplexer_6_out), .sel(\多周期硬布线控制器_1_pcsrc ));
  or or_1 (or_1_out, \多周期硬布线控制器_1_pcwrite , and_1_out, and_2_out);

  // Notes on the sheet:
  //   Ctrl+K  Command+K触发时钟连续仿真，程序运行结束后可停机，查看数据存储器中80单元的排序情况是有符号降序
  //   完成微程序模式的多周期CPU后，将主机架构图复制到本电路中，替换控制器为硬布线控制器
  //   存储器
  //   总周期数参考值：891
  //   MemWrite
  //   MemRead
  //   IorD
  //   IRWrite
  //   OP
  //   Func
  //   RegDst
  //   PcWrite
  //   Beq
  //   Bne
  //   PcSrc
  //   AluOP
  //   AluSrcB
  //   AluSrcA
  //   RegWrite
  //   MemToReg
endmodule

// 控制器状态机
module \状态机FSM  (
  input  S3,
  input  S2,
  input  S1,
  input  S0,
  input  R_Type,
  input  ADDI,
  input  LW,
  input  SW,
  input  BEQ,
  input  BNE,
  input  SYSCALL,
  output N3,
  output N2,
  output N1,
  output N0
);

  wire and_1_out, and_2_out, and_3_out, and_4_out, and_5_out, and_6_out, and_7_out, and_8_out, and_9_out,
       and_10_out, and_11_out, and_12_out, and_13_out, and_14_out, and_15_out, and_16_out, and_17_out,
       and_18_out, and_19_out, and_20_out, and_21_out, and_22_out, and_23_out, and_24_out, and_25_out,
       and_26_out, and_27_out, and_28_out, not_1_out, not_2_out, not_3_out, not_4_out, not_5_out, not_6_out,
       not_7_out, not_8_out, not_9_out, not_10_out, not_11_out, not_12_out, not_13_out, not_14_out,
       not_15_out, not_16_out, not_17_out, not_18_out, not_19_out, not_20_out, not_21_out, not_22_out,
       not_23_out, not_24_out, not_25_out, not_26_out, not_27_out, not_28_out, not_29_out, not_30_out,
       not_31_out, not_32_out, not_33_out, not_34_out, not_35_out, not_36_out, not_37_out, not_38_out,
       not_39_out, not_40_out, not_41_out, not_42_out, not_43_out, not_44_out, not_45_out, not_46_out,
       not_47_out, not_48_out, not_49_out, not_50_out, not_51_out, not_52_out, not_53_out, not_54_out,
       not_55_out, not_56_out, not_57_out, not_58_out, not_59_out, not_60_out, not_61_out, not_62_out,
       not_63_out, not_64_out, not_65_out, not_66_out, not_67_out, not_68_out, not_69_out, not_70_out;

  not not_1 (not_1_out, S3);
  not not_2 (not_2_out, S2);
  not not_3 (not_3_out, S1);
  not not_4 (not_4_out, S3);
  not not_5 (not_5_out, S2);
  not not_6 (not_6_out, S1);
  not not_7 (not_7_out, S3);
  not not_8 (not_8_out, S2);
  not not_9 (not_9_out, S1);
  not not_10 (not_10_out, S3);
  not not_11 (not_11_out, S2);
  not not_12 (not_12_out, S1);
  not not_13 (not_13_out, S3);
  not not_14 (not_14_out, S2);
  not not_15 (not_15_out, S1);
  not not_16 (not_16_out, S3);
  not not_17 (not_17_out, S2);
  not not_18 (not_18_out, S1);
  not not_19 (not_19_out, S3);
  not not_20 (not_20_out, S2);
  not not_21 (not_21_out, S1);
  not not_22 (not_22_out, S3);
  not not_23 (not_23_out, S2);
  not not_24 (not_24_out, S1);
  not not_25 (not_25_out, S3);
  not not_26 (not_26_out, S2);
  not not_27 (not_27_out, S3);
  not not_28 (not_28_out, S1);
  not not_29 (not_29_out, S2);
  not not_30 (not_30_out, S1);
  not not_31 (not_31_out, S3);
  not not_32 (not_32_out, S2);
  not not_33 (not_33_out, S1);
  not not_34 (not_34_out, S3);
  not not_35 (not_35_out, S2);
  not not_36 (not_36_out, S1);
  not not_37 (not_37_out, S3);
  not not_38 (not_38_out, S2);
  not not_39 (not_39_out, S1);
  not not_40 (not_40_out, S3);
  not not_41 (not_41_out, S2);
  not not_42 (not_42_out, S1);
  not not_43 (not_43_out, S3);
  not not_44 (not_44_out, S2);
  not not_45 (not_45_out, S0);
  not not_46 (not_46_out, S3);
  not not_47 (not_47_out, S1);
  not not_48 (not_48_out, S3);
  not not_49 (not_49_out, S2);
  not not_50 (not_50_out, S1);
  not not_51 (not_51_out, S0);
  not not_52 (not_52_out, S3);
  not not_53 (not_53_out, S2);
  not not_54 (not_54_out, S1);
  not not_55 (not_55_out, S3);
  not not_56 (not_56_out, S2);
  not not_57 (not_57_out, S1);
  not not_58 (not_58_out, S3);
  not not_59 (not_59_out, S2);
  not not_60 (not_60_out, S1);
  not not_61 (not_61_out, S3);
  not not_62 (not_62_out, S2);
  not not_63 (not_63_out, S1);
  not not_64 (not_64_out, S3);
  not not_65 (not_65_out, S2);
  not not_66 (not_66_out, S1);
  not not_67 (not_67_out, S3);
  not not_68 (not_68_out, S2);
  not not_69 (not_69_out, S0);
  not not_70 (not_70_out, S1);
  and and_1 (and_1_out, not_1_out, not_2_out, not_3_out, S0, BEQ);
  and and_2 (and_2_out, not_4_out, not_5_out, not_6_out, S0, BNE);
  and and_3 (and_3_out, not_7_out, not_8_out, not_9_out, S0, SYSCALL);
  and and_4 (and_4_out, not_10_out, not_11_out, not_12_out, S0, ADDI);
  and and_5 (and_5_out, not_13_out, S2, S1, S0);
  and and_6 (and_6_out, S3, not_14_out, S1, S0);
  and and_7 (and_7_out, S3, S2, not_15_out, S0);
  and and_8 (and_8_out, not_16_out, not_17_out, not_18_out, S0, R_Type);
  and and_9 (and_9_out, not_19_out, not_20_out, not_21_out, S0, SW);
  and and_10 (and_10_out, not_22_out, not_23_out, not_24_out, S0, SYSCALL);
  and and_11 (and_11_out, not_25_out, not_26_out, S1, S0);
  and and_12 (and_12_out, not_27_out, S2, not_28_out, S0);
  and and_13 (and_13_out, S3, not_29_out, S1, S0);
  and and_14 (and_14_out, S3, S2, not_30_out, S0);
  and and_15 (and_15_out, not_31_out, not_32_out, not_33_out, S0, R_Type);
  and and_16 (and_16_out, not_34_out, not_35_out, not_36_out, S0, LW);
  and and_17 (and_17_out, not_37_out, not_38_out, not_39_out, S0, BNE);
  and and_18 (and_18_out, not_40_out, not_41_out, not_42_out, S0, ADDI);
  and and_19 (and_19_out, not_43_out, not_44_out, S1, not_45_out);
  and and_20 (and_20_out, not_46_out, S2, not_47_out, S0);
  and and_21 (and_21_out, not_48_out, not_49_out, not_50_out, not_51_out);
  and and_22 (and_22_out, not_52_out, not_53_out, not_54_out, S0, R_Type);
  and and_23 (and_23_out, not_55_out, not_56_out, not_57_out, S0, SW);
  and and_24 (and_24_out, not_58_out, not_59_out, not_60_out, S0, BEQ);
  and and_25 (and_25_out, not_61_out, not_62_out, not_63_out, S0, SYSCALL);
  and and_26 (and_26_out, not_64_out, not_65_out, not_66_out, S0, ADDI);
  and and_27 (and_27_out, not_67_out, not_68_out, S1, not_69_out);
  and and_28 (and_28_out, S3, S2, not_70_out, S0);
  or or_1 (N3, and_1_out, and_2_out, and_3_out, and_4_out, and_5_out, and_6_out, and_7_out);
  or or_2 (N2, and_8_out, and_9_out, and_10_out, and_11_out, and_12_out, and_13_out, and_14_out);
  or or_3 (N1, and_15_out, and_16_out, and_17_out, and_18_out, and_19_out, and_20_out);
  or or_4 (N0, and_21_out, and_22_out, and_23_out, and_24_out, and_25_out, and_26_out, and_27_out, and_28_out);
endmodule

module MIPS_Regifile (
  input  [31:0] Din,
  input  Clk,
  input  WE,
  input  [4:0] R1_num,
  input  [4:0] W_num,
  input  [4:0] R2_num,
  output [31:0] R1,
  output [31:0] R2
);

  // RegisterFile registerfile_1: pin names not known; wires that end beside it: Din, Clk, WE, W_num, R1_num, R2_num, R1, R2
endmodule

// ALU
module MIPS_ALU (
  input  [31:0] X,
  input  [31:0] Y,
  input  [3:0] AluOP,
  output Equal,
  output [31:0] Result,
  output [31:0] Result_2
);

  wire [0:0] comparator_1_lt, comparator_2_lt;
  wire [31:0] adder_1_out, AND_out, divider_1_out, divider_1_rem, multiplier_1_cout, multiplier_1_out,
       NOR_out, OR_out, shifter_1_out, shifter_2_out, shifter_3_out, subtractor_1_out, XOR_out;

  Shifter #(.width(32)) shifter_1 (.in(X), .\dist (Y[4:0]), .out(shifter_1_out));
  Shifter #(.width(32), .shift("ar")) shifter_2 (.in(X), .\dist (Y[4:0]), .out(shifter_2_out));
  Shifter #(.width(32), .shift("lr")) shifter_3 (.in(X), .\dist (Y[4:0]), .out(shifter_3_out));
  Multiplier #(.width(32)) multiplier_1 (.a(X), .b(Y), .out(multiplier_1_out), .cout(multiplier_1_cout));  // open: cin
  Divider #(.width(32)) divider_1 (.a(X), .b(Y), .out(divider_1_out), .rem(divider_1_rem));  // open: upper
  Adder #(.width(32)) adder_1 (.a(X), .b(Y), .out(adder_1_out));  // open: cin, cout
  Subtractor #(.width(32)) subtractor_1 (.a(X), .b(Y), .out(subtractor_1_out));  // open: bin, bout
  assign AND_out = X & Y;  // AND_Gate AND, 32 bits wide
  assign OR_out = X | Y;  // OR_Gate OR, 32 bits wide
  assign XOR_out = X ^ Y;  // XOR_Gate XOR, 32 bits wide
  assign NOR_out = ~(X | Y);  // NOR_Gate NOR, 32 bits wide
  Comparator #(.width(32)) comparator_1 (.a(X), .b(Y), .eq(Equal), .lt(comparator_1_lt[0]));  // open: gt
  Comparator #(.width(32)) comparator_2 (.a(X), .b(Y), .lt(comparator_2_lt[0]));  // open: gt, eq
  Multiplexer #(.select(4), .width(32), .enable("false")) multiplexer_1 (
    .in0(shifter_1_out), .in1(shifter_2_out), .in2(shifter_3_out), .in3(multiplier_1_out),
    .in4(divider_1_out), .in5(adder_1_out), .in6(subtractor_1_out), .in7(AND_out), .in8(OR_out),
    .in9(XOR_out), .in10(NOR_out), .in11({{31{1'b0}}, comparator_1_lt[0]}),
    .in12({{31{1'b0}}, comparator_2_lt[0]}), .in13({32{1'b0}}), .in14({32{1'b0}}), .in15({32{1'b0}}),
    .out(Result), .sel(AluOP));
  Multiplexer #(.select(4), .width(32), .enable("false")) multiplexer_2 (
    .in0({32{1'b0}}), .in1({32{1'b0}}), .in2({32{1'b0}}), .in3(multiplier_1_cout), .in4(divider_1_rem),
    .in5({32{1'b0}}), .in6({32{1'b0}}), .in7({32{1'b0}}), .in8({32{1'b0}}), .in9({32{1'b0}}),
    .in10({32{1'b0}}), .in11({32{1'b0}}), .in12({32{1'b0}}), .in13({32{1'b0}}), .in14({32{1'b0}}),
    .in15({32{1'b0}}), .out(Result_2), .sel(AluOP));

  // Other names for the same wires on the sheet: Result2[31:0] = Result_2; S[3:0] = AluOP

  // Notes on the sheet:
  //   不要改变此引脚区域内容，也不要改变ALU封装形式
  //   输入引脚
  //   输出引脚
endmodule

// 硬布线控器
module \多周期硬布线控制器  (
  input  [5:0] OP,
  input  [5:0] Func,
  input  CLK,
  input  RST,
  output [3:0] ALU_OP,
  output Bne,
  output Beq,
  output MemRead,
  output MemWrite,
  output RegWrite,
  output PcWrite,
  output IrWrite,
  output RegDst,
  output MemToReg,
  output [3:0] \当前状态 ,
  output [1:0] AluSrcB,
  output AluSrcA,
  output PCsrc,
  output IorD
);

  wire ADD, ADDI, BEQ_t, BNE_t, comparator_6_eq, comparator_7_eq, comparator_8_eq, comparator_9_eq, LW, P,
       R_TYPE, SLT, SW, SysCall;
  wire [1:0] ALU_Control;
  wire [3:0] multiplexer_1_out, rom_1_data, \状态机fsm_1_n0 ;

  Comparator #(.width(6)) comparator_1 (.a(OP), .b(6'b100011), .eq(LW));  // open: gt, lt
  Comparator #(.width(6)) comparator_2 (.a(OP), .b(6'b101011), .eq(SW));  // open: gt, lt
  Comparator #(.width(6)) comparator_3 (.a(OP), .b(6'b000100), .eq(BEQ_t));  // open: gt, lt
  Comparator #(.width(6)) comparator_4 (.a(OP), .b(6'b000101), .eq(BNE_t));  // open: gt, lt
  Comparator #(.width(6)) comparator_5 (.a(OP), .b(6'b001000), .eq(ADDI));  // open: gt, lt
  Comparator #(.width(6)) comparator_6 (.a(OP), .b({6{1'b0}}), .eq(comparator_6_eq));  // open: gt, lt
  \状态机FSM  \u_状态机fsm_1  (
    .S3(\当前状态 [3]), .S2(\当前状态 [2]), .S1(\当前状态 [1]), .S0(\当前状态 [0]), .R_Type(R_TYPE), .ADDI(ADDI), .LW(LW),
    .N3(\状态机fsm_1_n0 [3]), .SW(SW), .BEQ(BEQ_t), .BNE(BNE_t), .SYSCALL(SysCall), .N2(\状态机fsm_1_n0 [2]),
    .N1(\状态机fsm_1_n0 [1]), .N0(\状态机fsm_1_n0 [0]));
  Comparator #(.width(6)) comparator_7 (.a(Func), .b(6'b100000), .eq(comparator_7_eq));  // open: gt, lt
  Comparator #(.width(6)) comparator_8 (.a(Func), .b(6'b101010), .eq(comparator_8_eq));  // open: gt, lt
  Comparator #(.width(6)) comparator_9 (.a(Func), .b(6'b001100), .eq(comparator_9_eq));  // open: gt, lt
  and and_1 (ADD, comparator_7_eq, comparator_6_eq);
  and and_2 (SLT, comparator_8_eq, comparator_6_eq);
  and and_3 (SysCall, comparator_9_eq, comparator_6_eq);
  Register #(.width(4)) register_1 (.D(\状态机fsm_1_n0 ), .Q(\当前状态 ), .clk(CLK), .clr(RST));  // open: en
  or or_1 (R_TYPE, ADD, SLT);
  ROM #(.addrWidth(4), .dataWidth(21)) rom_1 (
    .addr(\当前状态 ),
    .data({IorD, PCsrc, AluSrcA, AluSrcB, MemToReg, RegDst, IrWrite, PcWrite, RegWrite, MemWrite, MemRead, Beq, Bne, ALU_Control, P, rom_1_data}));  // open: sel
  Multiplexer #(.select(2), .width(4), .enable("false")) multiplexer_1 (
    .in0(4'b0000), .in1(4'b0101), .in2(4'b1011), .in3(4'b0000), .out(multiplexer_1_out), .sel({SLT, ADD}));
  Multiplexer #(.select(2), .width(4), .enable("false")) multiplexer_2 (
    .in0(4'b0101), .in1(4'b0110), .in2(multiplexer_1_out), .in3(4'b0000), .out(ALU_OP), .sel(ALU_Control));

  // Notes on the sheet:
  //   指令译码信号
  //   现态
  //   组合逻辑
  //   指令译码逻辑
  //   次态
  //   状态寄存器
  //   控制存储器
  //   contents of rom_1 (hex, n*v repeats v):
  //   13201 30010 60003 100204 8800 60006 100400 40048 4800 c0120 c00a0 6000c 800 d
  //   ALU控制器逻辑
  //   根据ALU_Control的值决定运算器运算选择控制信号ALU_OP的值
  //   ALU_Control= 00 运算器做加法
  //   ALU_Control= 01 运算器做减法
  //   ALU_Control= 10 运算方式由Func决定 
endmodule

module \多周期MIPS_纯硬布线  (
);

  wire and_1_out, and_2_out, CLK, comparator_1_eq, mips_alu_1_equal, not_1_out, not_2_out, or_1_out, RST,
       \多周期纯硬布线控制器_1_alusrca , \多周期纯硬布线控制器_1_beq , \多周期纯硬布线控制器_1_bne , \多周期纯硬布线控制器_1_iord ,
       \多周期纯硬布线控制器_1_irwrite , \多周期纯硬布线控制器_1_memread , \多周期纯硬布线控制器_1_memtoreg , \多周期纯硬布线控制器_1_memwrite ,
       \多周期纯硬布线控制器_1_pcsrc , \多周期纯硬布线控制器_1_pcwrite , \多周期纯硬布线控制器_1_regdst , \多周期纯硬布线控制器_1_regwrite ;
  wire [1:0] \多周期纯硬布线控制器_1_alusrcb ;
  wire [3:0] \多周期纯硬布线控制器_1_alu_op , \多周期纯硬布线控制器_1_当前状态 ;
  wire [4:0] multiplexer_2_out;
  wire [15:0] \总周期数 ;
  wire [31:0] A_q, B_q, bit_extender_1_out, C_q, DR_q, IR_q, mips_alu_1_result, mips_regifile_1_r1,
       mips_regifile_1_r2, multiplexer_1_out, multiplexer_3_out, multiplexer_4_out, multiplexer_5_out,
       multiplexer_6_out, PC_q, ram_1_data, shifter_1_out;

  Button \u_总复位  (.out(RST));
  Register #(.width(32)) PC (.D(multiplexer_6_out), .en(or_1_out), .Q(PC_q), .clk(CLK), .clr(RST));
  Clock clock_1 (.out(CLK));
  Multiplexer #(.width(32), .enable("false")) multiplexer_1 (
    .in0(PC_q), .in1(C_q), .out(multiplexer_1_out), .sel(\多周期纯硬布线控制器_1_iord ));
  RAM #(.addrWidth(10), .dataWidth(32), .bus("separate")) ram_1 (
    .addr(multiplexer_1_out[11:2]), .din(B_q), .data(ram_1_data), .str(\多周期纯硬布线控制器_1_memwrite ), .clk(CLK),
    .ld(\多周期纯硬布线控制器_1_memread ));  // open: sel, clr
  // Probe on \总周期数 
  Register #(.width(32)) IR (.D(ram_1_data), .en(\多周期纯硬布线控制器_1_irwrite ), .Q(IR_q), .clk(CLK), .clr(RST));
  Register #(.width(32)) DR (.D(ram_1_data), .Q(DR_q), .clk(CLK), .clr(RST));  // open: en
  // Probe on \多周期纯硬布线控制器_1_当前状态 
  Multiplexer #(.width(5), .enable("false")) multiplexer_2 (
    .in0(IR_q[20:16]), .in1(IR_q[15:11]), .out(multiplexer_2_out), .sel(\多周期纯硬布线控制器_1_regdst ));
  assign bit_extender_1_out = {{16{IR_q[15]}}, IR_q[15:0]};  // Bit_Extender bit_extender_1
  \多周期纯硬布线控制器  \u_多周期纯硬布线控制器_1  (
    .OP(IR_q[31:26]), .Func(IR_q[5:0]), .ALU_OP(\多周期纯硬布线控制器_1_alu_op ), .CLK(CLK), .RST(RST),
    .\当前状态 (\多周期纯硬布线控制器_1_当前状态 ), .IorD(\多周期纯硬布线控制器_1_iord ), .PCsrc(\多周期纯硬布线控制器_1_pcsrc ),
    .AluSrcA(\多周期纯硬布线控制器_1_alusrca ), .AluSrcB(\多周期纯硬布线控制器_1_alusrcb ), .MemToReg(\多周期纯硬布线控制器_1_memtoreg ),
    .RegDst(\多周期纯硬布线控制器_1_regdst ), .IrWrite(\多周期纯硬布线控制器_1_irwrite ), .PcWrite(\多周期纯硬布线控制器_1_pcwrite ),
    .RegWrite(\多周期纯硬布线控制器_1_regwrite ), .MemWrite(\多周期纯硬布线控制器_1_memwrite ), .MemRead(\多周期纯硬布线控制器_1_memread ),
    .Beq(\多周期纯硬布线控制器_1_beq ), .Bne(\多周期纯硬布线控制器_1_bne ));
  Multiplexer #(.width(32), .enable("false")) multiplexer_3 (
    .in0(C_q), .in1(DR_q), .out(multiplexer_3_out), .sel(\多周期纯硬布线控制器_1_memtoreg ));
  Comparator #(.width(4)) comparator_1 (.a(4'b1101), .b(\多周期纯硬布线控制器_1_当前状态 ), .eq(comparator_1_eq));  // open: gt, lt
  MIPS_Regifile mips_regifile_1 (
    .Din(multiplexer_3_out), .Clk(CLK), .R1(mips_regifile_1_r1), .R2(mips_regifile_1_r2),
    .WE(\多周期纯硬布线控制器_1_regwrite ), .W_num(multiplexer_2_out), .R1_num(IR_q[25:21]), .R2_num(IR_q[20:16]));
  Counter #(.width(16), .max('hffff)) counter_1 (
    .count(not_1_out), .Q(\总周期数 ), .clk(CLK), .clr(RST));  // open: load, D, carry
  not not_1 (not_1_out, comparator_1_eq);
  Register #(.width(32)) A (.D(mips_regifile_1_r1), .Q(A_q), .clk(CLK), .clr(RST));  // open: en
  Register #(.width(32)) B (.D(mips_regifile_1_r2), .Q(B_q), .clk(CLK), .clr(RST));  // open: en
  Multiplexer #(.width(32), .enable("false")) multiplexer_4 (
    .in0(PC_q), .in1(A_q), .out(multiplexer_4_out), .sel(\多周期纯硬布线控制器_1_alusrca ));
  Shifter #(.width(32)) shifter_1 (.in(bit_extender_1_out), .\dist (5'b00010), .out(shifter_1_out));
  Multiplexer #(.select(2), .width(32), .enable("false")) multiplexer_5 (
    .in0(B_q), .in1(32'h4), .in2(bit_extender_1_out), .in3(shifter_1_out), .out(multiplexer_5_out),
    .sel(\多周期纯硬布线控制器_1_alusrcb ));
  MIPS_ALU mips_alu_1 (
    .X(multiplexer_4_out), .Y(multiplexer_5_out), .AluOP(\多周期纯硬布线控制器_1_alu_op ), .Equal(mips_alu_1_equal),
    .Result(mips_alu_1_result));  // open: Result_2
  not not_2 (not_2_out, mips_alu_1_equal);
  Register #(.width(32)) C (.D(mips_alu_1_result), .Q(C_q), .clk(CLK), .clr(RST));  // open: en
  and and_1 (and_1_out, \多周期纯硬布线控制器_1_beq , mips_alu_1_equal);
  and and_2 (and_2_out, \多周期纯硬布线控制器_1_bne , not_2_out);
  Multiplexer #(.width(32), .enable("false")) multiplexer_6 (
    .in0(mips_alu_1_result), .in1(C_q), .out(multiplexer_6_out), .sel(\多周期纯硬布线控制器_1_pcsrc ));
  or or_1 (or_1_out, \多周期纯硬布线控制器_1_pcwrite , and_1_out, and_2_out);

  // Notes on the sheet:
  //   Ctrl+K  Command+K触发时钟连续仿真，程序运行结束后可停机，查看数据存储器中80单元的排序情况是有符号降序
  //   完成微程序模式的多周期CPU后，将主机架构图复制到本电路中，替换控制器为硬布线控制器
  //   存储器
  //   总周期数参考值：891
  //   IorD
  //   MemWrite
  //   MemRead
  //   IRWrite
  //   OP
  //   Func
  //   RegDst
  //   PcWrite
  //   Beq
  //   Bne
  //   PcSrc
  //   AluOP
  //   AluSrcB
  //   AluSrcA
  //   RegWrite
  //   MemToReg
endmodule

// 纯硬布线控制器
module \多周期纯硬布线控制器  (
  input  [5:0] OP,
  input  [5:0] Func,
  input  CLK,
  input  RST,
  output IorD,
  output [3:0] ALU_OP,
  output PCsrc,
  output AluSrcA,
  output [1:0] AluSrcB,
  output MemToReg,
  output RegDst,
  output IrWrite,
  output PcWrite,
  output RegWrite,
  output MemWrite,
  output [3:0] \当前状态 ,
  output MemRead,
  output Beq,
  output Bne
);

  wire ADD, ADDI, BEQ_t, BNE_t, comparator_6_eq, comparator_7_eq, comparator_8_eq, comparator_9_eq, LW,
       R_TYPE, SLT, SW, SysCall;
  wire [1:0] ALU_Control;
  wire [3:0] multiplexer_1_out, \状态机fsm_1_n0 ;

  Comparator #(.width(6)) comparator_1 (.a(OP), .b(6'b100011), .eq(LW));  // open: gt, lt
  Comparator #(.width(6)) comparator_2 (.a(OP), .b(6'b101011), .eq(SW));  // open: gt, lt
  Comparator #(.width(6)) comparator_3 (.a(OP), .b(6'b000100), .eq(BEQ_t));  // open: gt, lt
  Comparator #(.width(6)) comparator_4 (.a(OP), .b(6'b000101), .eq(BNE_t));  // open: gt, lt
  Comparator #(.width(6)) comparator_5 (.a(OP), .b(6'b001000), .eq(ADDI));  // open: gt, lt
  Comparator #(.width(6)) comparator_6 (.a(OP), .b({6{1'b0}}), .eq(comparator_6_eq));  // open: gt, lt
  \状态机FSM  \u_状态机fsm_1  (
    .S3(\当前状态 [3]), .S2(\当前状态 [2]), .S1(\当前状态 [1]), .S0(\当前状态 [0]), .R_Type(R_TYPE), .ADDI(ADDI), .LW(LW),
    .N3(\状态机fsm_1_n0 [3]), .SW(SW), .BEQ(BEQ_t), .BNE(BNE_t), .SYSCALL(SysCall), .N2(\状态机fsm_1_n0 [2]),
    .N1(\状态机fsm_1_n0 [1]), .N0(\状态机fsm_1_n0 [0]));
  Comparator #(.width(6)) comparator_7 (.a(Func), .b(6'b100000), .eq(comparator_7_eq));  // open: gt, lt
  Comparator #(.width(6)) comparator_8 (.a(Func), .b(6'b101010), .eq(comparator_8_eq));  // open: gt, lt
  Comparator #(.width(6)) comparator_9 (.a(Func), .b(6'b001100), .eq(comparator_9_eq));  // open: gt, lt
  and and_1 (ADD, comparator_7_eq, comparator_6_eq);
  and and_2 (SLT, comparator_8_eq, comparator_6_eq);
  and and_3 (SysCall, comparator_9_eq, comparator_6_eq);
  Register #(.width(4)) register_1 (.D(\状态机fsm_1_n0 ), .Q(\当前状态 ), .clk(CLK), .clr(RST));  // open: en
  or or_1 (R_TYPE, ADD, SLT);
  \纯硬布线控制器实现1  \u_纯硬布线控制器实现1_1  (
    .S3(\当前状态 [3]), .S2(\当前状态 [2]), .S1(\当前状态 [1]), .S0(\当前状态 [0]), .N3(IorD), .N2(PCsrc), .N1(AluSrcA),
    .N0(AluSrcB[1]));
  \纯硬布线控制器实现2  \u_纯硬布线控制器实现2_1  (
    .S3(\当前状态 [3]), .S2(\当前状态 [2]), .S1(\当前状态 [1]), .S0(\当前状态 [0]), .N3(AluSrcB[0]), .N2(MemToReg),
    .N1(RegDst), .N0(IrWrite));
  \纯硬布线控制器实现3  \u_纯硬布线控制器实现3_1  (
    .S3(\当前状态 [3]), .S2(\当前状态 [2]), .S1(\当前状态 [1]), .S0(\当前状态 [0]), .N3(PcWrite), .N2(RegWrite),
    .N1(MemWrite), .N0(MemRead));
  \纯硬布线控制器实现4  \u_纯硬布线控制器实现4_1  (
    .S3(\当前状态 [3]), .S2(\当前状态 [2]), .S1(\当前状态 [1]), .S0(\当前状态 [0]), .N3(Beq), .N2(Bne), .N1(ALU_Control[1]),
    .N0(ALU_Control[0]));
  Multiplexer #(.select(2), .width(4), .enable("false")) multiplexer_1 (
    .in0(4'b0000), .in1(4'b0101), .in2(4'b1011), .in3(4'b0000), .out(multiplexer_1_out), .sel({SLT, ADD}));
  Multiplexer #(.select(2), .width(4), .enable("false")) multiplexer_2 (
    .in0(4'b0101), .in1(4'b0110), .in2(multiplexer_1_out), .in3(4'b0000), .out(ALU_OP), .sel(ALU_Control));

  // Notes on the sheet:
  //   指令译码信号
  //   现态
  //   组合逻辑
  //   指令译码逻辑
  //   次态
  //   状态寄存器
  //   ALU控制器逻辑
  //   根据ALU_Control的值决定运算器运算选择控制信号ALU_OP的值
  //   ALU_Control= 00 运算器做加法
  //   ALU_Control= 01 运算器做减法
  //   ALU_Control= 10 运算方式由Func决定 
endmodule

module \纯硬布线控制器实现1  (
  input  S3,
  input  S2,
  input  S1,
  input  S0,
  output N3,
  output N2,
  output N1,
  output N0
);

  wire and_1_out, and_2_out, and_3_out, and_4_out, and_5_out, and_6_out, and_7_out, and_8_out, and_9_out,
       and_10_out, and_11_out, and_12_out, and_13_out, and_14_out, not_1_out, not_2_out, not_3_out,
       not_4_out, not_5_out, not_6_out, not_7_out, not_8_out, not_9_out, not_10_out, not_11_out, not_12_out,
       not_13_out, not_14_out, not_15_out;

  not not_1 (not_1_out, S3);
  not not_2 (not_2_out, S2);
  not not_3 (not_3_out, S0);
  not not_4 (not_4_out, S2);
  not not_5 (not_5_out, S1);
  not not_6 (not_6_out, S0);
  not not_7 (not_7_out, S2);
  and and_1 (and_1_out, not_7_out, S1, not_8_out);
  not not_8 (not_8_out, S0);
  not not_9 (not_9_out, S3);
  and and_2 (and_2_out, not_9_out, S2, S0);
  not not_10 (not_10_out, S2);
  and and_3 (and_3_out, S3, not_10_out, S0);
  and and_4 (and_4_out, S3, S1);
  not not_11 (not_11_out, S3);
  not not_12 (not_12_out, S1);
  not not_13 (not_13_out, S3);
  not not_14 (not_14_out, S2);
  not not_15 (not_15_out, S0);
  and and_5 (and_5_out, not_1_out, not_2_out, S1, S0);
  and and_6 (and_6_out, S2, S1, not_3_out);
  or or_1 (N3, and_5_out, and_6_out, and_7_out);
  and and_7 (and_7_out, S3, S2, S1);
  and and_8 (and_8_out, S3, not_4_out, not_5_out, S0);
  or or_2 (N2, and_8_out, and_9_out, and_10_out);
  and and_9 (and_9_out, S3, S1, not_6_out);
  and and_10 (and_10_out, S3, S2, S1);
  or or_3 (N1, and_1_out, and_2_out, and_3_out, and_4_out);
  and and_11 (and_11_out, not_11_out, not_12_out, S0);
  and and_12 (and_12_out, not_13_out, not_14_out, S1, not_15_out);
  and and_13 (and_13_out, S3, S1, S0);
  and and_14 (and_14_out, S3, S2, S1);
  or or_4 (N0, and_11_out, and_12_out, and_13_out, and_14_out);
endmodule

module \纯硬布线控制器实现2  (
  input  S3,
  input  S2,
  input  S1,
  input  S0,
  output N3,
  output N2,
  output N1,
  output N0
);

  wire and_1_out, and_2_out, and_3_out, and_4_out, and_5_out, and_6_out, and_7_out, and_8_out, and_9_out,
       and_10_out, not_1_out, not_2_out, not_3_out, not_4_out, not_5_out, not_6_out, not_7_out, not_8_out,
       not_9_out, not_10_out, not_11_out, not_12_out, not_13_out, not_14_out, not_15_out;

  not not_1 (not_1_out, S1);
  and and_1 (and_1_out, not_1_out, not_2_out);
  not not_2 (not_2_out, S0);
  not not_3 (not_3_out, S3);
  not not_4 (not_4_out, S2);
  and and_2 (and_2_out, not_3_out, not_4_out, S0);
  and and_3 (and_3_out, S2, not_5_out);
  not not_5 (not_5_out, S0);
  and and_4 (and_4_out, S3, S2);
  not not_6 (not_6_out, S3);
  not not_7 (not_7_out, S1);
  not not_8 (not_8_out, S0);
  not not_9 (not_9_out, S2);
  not not_10 (not_10_out, S1);
  not not_11 (not_11_out, S0);
  not not_12 (not_12_out, S3);
  not not_13 (not_13_out, S2);
  not not_14 (not_14_out, S1);
  not not_15 (not_15_out, S0);
  or or_1 (N3, and_1_out, and_2_out, and_3_out, and_4_out);
  and and_5 (and_5_out, not_6_out, S2, not_7_out, not_8_out);
  or or_2 (N2, and_5_out, and_6_out);
  and and_6 (and_6_out, S3, S2, S1);
  and and_7 (and_7_out, S3, not_9_out, not_10_out, not_11_out);
  or or_3 (N1, and_7_out, and_8_out);
  and and_8 (and_8_out, S3, S2, S1);
  and and_9 (and_9_out, not_12_out, not_13_out, not_14_out, not_15_out);
  or or_4 (N0, and_9_out, and_10_out);
  and and_10 (and_10_out, S3, S2, S1);
endmodule

module \纯硬布线控制器实现3  (
  input  S3,
  input  S2,
  input  S1,
  input  S0,
  output N3,
  output N2,
  output N1,
  output N0
);

  wire and_1_out, and_2_out, and_3_out, and_5_out, and_6_out, and_7_out, and_8_out, and_9_out, not_1_out,
       not_2_out, not_3_out, not_4_out, not_5_out, not_6_out, not_7_out, not_8_out, not_9_out, not_10_out,
       not_11_out, not_12_out, not_13_out, not_14_out, not_15_out;

  not not_1 (not_1_out, S3);
  not not_2 (not_2_out, S2);
  not not_3 (not_3_out, S1);
  not not_4 (not_4_out, S0);
  not not_5 (not_5_out, S1);
  and and_1 (and_1_out, S2, not_5_out, not_6_out);
  not not_6 (not_6_out, S0);
  and and_2 (and_2_out, S3, not_7_out, not_8_out);
  not not_7 (not_7_out, S1);
  not not_8 (not_8_out, S0);
  and and_3 (and_3_out, S3, S2, S1);
  and and_4 (N1, S2, S1, not_9_out);
  not not_9 (not_9_out, S0);
  not not_10 (not_10_out, S3);
  not not_11 (not_11_out, S2);
  not not_12 (not_12_out, S1);
  not not_13 (not_13_out, S0);
  not not_14 (not_14_out, S3);
  not not_15 (not_15_out, S2);
  and and_5 (and_5_out, not_1_out, not_2_out, not_3_out, not_4_out);
  or or_1 (N3, and_5_out, and_6_out);
  and and_6 (and_6_out, S3, S2, S1);
  or or_2 (N2, and_1_out, and_2_out, and_3_out);
  and and_7 (and_7_out, not_10_out, not_11_out, not_12_out, not_13_out);
  or or_3 (N0, and_7_out, and_8_out, and_9_out);
  and and_8 (and_8_out, not_14_out, not_15_out, S1, S0);
  and and_9 (and_9_out, S3, S2, S1);
endmodule

module \纯硬布线控制器实现4  (
  input  S3,
  input  S2,
  input  S1,
  input  S0,
  output N3,
  output N2,
  output N1,
  output N0
);

  wire and_4_out, and_5_out, and_6_out, not_1_out, not_2_out, not_3_out, not_4_out, not_5_out, not_6_out;

  not not_1 (not_1_out, S2);
  not not_2 (not_2_out, S1);
  and and_1 (N2, S3, S1, not_3_out);
  not not_3 (not_3_out, S0);
  not not_4 (not_4_out, S2);
  not not_5 (not_5_out, S1);
  not not_6 (not_6_out, S0);
  and and_2 (N0, S3, S2, S1, S0);
  and and_3 (N3, S3, not_1_out, not_2_out, S0);
  and and_4 (and_4_out, S2, S1, S0);
  or or_1 (N1, and_4_out, and_5_out, and_6_out);
  and and_5 (and_5_out, S3, not_4_out, not_5_out, not_6_out);
  and and_6 (and_6_out, S3, S2, S1);
endmodule
